# Fritzing sketch Capteur PAR (saved by Fritzing 0.9.3b)
circuit board: 2.24946cm x 2.49418cm
breadboards: 2

parts:
  J1 = male pin header, 2 pins [form="♂ (male)"]
  J2 = male pin header, 2 pins [form="♂ (male)"]
  J3 = male pin header, 2 pins [form="♂ (male)"]
  J4 = male pin header, 2 pins [form="♂ (male)"]
  C1 = Electrolytic Capacitor [capacitance=100nF package="100 mil [THT, electrolytic]"]
  IC1 = TLS230RD
  CTN = Temperature Sensor (Thermistor) [thermistor_type=NTC package=THT]
  J5 = male pin header, 5 pins [form="♂ (male)"]

nets:
  N1: J1.pin1, IC1.S3
  N2: J1.pin2, J2.pin1, J3.pin2, J4.pin1, C1.+, IC1.VDD, J5.pin1
  N3: J2.pin2, IC1.S1
  N4: J3.pin1, IC1.S0
  N5: J4.pin2, IC1.S2
  N6: C1.-, IC1.OE, IC1.GND, J5.pin3
  N7: IC1.OUT, J5.pin2
  N8: CTN.pin_0, J5.pin4
  N9: CTN.pin_1, J5.pin5

notes:
  S1
  S0
  S3
  S2
  Par Sensor
  v1.2
  A0
  GND
  R+
  VCC
  R-

custom parts:
  TLS230RD: The TSL230RD, TSL230ARD, and TSL230BRD programmable light-to-frequency converters combine a configurable silicon photodiode and a current-to-frequency converter on single monolithic CMOS integrated circuit. The output can be either a pulse train or a square wave (50% duty cycle) with frequency directly proportional to light intensity. Device sensitivity is selectable in three ranges, providing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
