# Fritzing sketch Pont Diviseur univesel (saved by Fritzing 0.9.3b)
circuit board: 1.90606cm x 1.14481cm
breadboards: 1

parts:
  R2 = Resistor [tolerance=±5% resistance=82k package=THT]
  R1 = Resistor [tolerance=±1% resistance=47k package=THT]
  J1 = male pin header, 3 pins [form="♂ (male)"]
  J2 = male pin header, 1 pin [form="♂ (male)"]  # not connected
  J3 = male pin header, 1 pin [form="♂ (male)"]  # not connected
  J4 = male pin header, 1 pin [form="♂ (male)"]  # not connected
  J5 = male pin header, 1 pin [form="♂ (male)"]  # not connected

nets:
  GND: R2.Pin_0, J1.pin1
  N1: R2.Pin_1, R1.Pin_0, J1.pin2
  5V: R1.Pin_1, J1.pin3

notes:
  + A0 -
  Pont Diviseur v1.1
  ~3.178V
